// Logisim project File with working 32 bit Register.circ as structural Verilog: 10 circuits, main circuit Logic Unit
module Logic_Unit (
  input  [1:0] OPCODE,
  input  [31:0] A,
  input  [31:0] B,
  output [31:0] OUTPUT
);

  wire [31:0] and_1_out, nor_1_out, or_1_out, xor_1_out;

  assign and_1_out = A & B;  // AND_Gate and_1, 32 bits wide
  assign or_1_out = A | B;  // OR_Gate or_1, 32 bits wide
  assign nor_1_out = ~(A | B);  // NOR_Gate nor_1, 32 bits wide
  assign xor_1_out = A ^ B;  // XOR_Gate xor_1, 32 bits wide
  Multiplexer #(.select(2), .width(32)) multiplexer_1 (
    .in0(and_1_out), .in1(or_1_out), .in2(nor_1_out), .in3(xor_1_out), .out(OUTPUT), .sel(OPCODE));  // open: en
endmodule

module Shifter (
  input  [31:0] A_LSB_5,
  input  [31:0] B,
  input  [1:0] OPCODE,
  output [31:0] OUTPUT
);

  wire [31:0] shifter_1_out, shifter_2_out, shifter_3_out;

  Shifter_part #(.width(32)) shifter_1 (.in(B), .\dist (A_LSB_5[4:0]), .out(shifter_1_out));
  Shifter_part #(.width(32), .shift("lr")) shifter_2 (.in(B), .\dist (A_LSB_5[4:0]), .out(shifter_2_out));
  Shifter_part #(.width(32), .shift("ar")) shifter_3 (.in(B), .\dist (A_LSB_5[4:0]), .out(shifter_3_out));
  Multiplexer #(.select(2), .width(32)) multiplexer_1 (
    .in0(B), .in1(shifter_1_out), .in2(shifter_2_out), .in3(shifter_3_out), .out(OUTPUT), .sel(OPCODE));  // open: en
endmodule

module Main_ALU (
  input  [1:0] OPCODE,
  input  [31:0] A,
  input  ADDER_OPCODE,
  input  [1:0] OPERATION_OPCODE,
  input  [31:0] B,
  output [31:0] out_6
);

  wire comparator_1_output;
  wire [31:0] adder_1_output, bit_extender_1_out, logic_unit_1_output, nor_1_out, shifter_1_output;

  Shifter shifter_1 (.A_LSB_5(A), .B(B), .OPCODE(OPCODE), .OUTPUT(shifter_1_output));
  Logic_Unit logic_unit_1 (.A(A), .B(B), .OPCODE(OPCODE), .OUTPUT(logic_unit_1_output));
  Comparator comparator_1 (.A(A), .B(B), .OUTPUT(comparator_1_output));
  Adder adder_1 (.A(A), .B(B), .OPCODE(ADDER_OPCODE), .OUTPUT(adder_1_output));
  assign bit_extender_1_out = {{31{1'b0}}, comparator_1_output};  // Bit_Extender bit_extender_1
  Multiplexer #(.select(2), .width(32)) multiplexer_1 (
    .in0(shifter_1_output), .in1(bit_extender_1_out), .in2(adder_1_output), .in3(logic_unit_1_output),
    .out(out_6), .sel(OPERATION_OPCODE));  // open: en
  assign nor_1_out = ~out_6;  // NOR_Gate nor_1, 32 bits wide NOR_Gate

  // Notes on the sheet:
  //   Comparator
  //   Adder
  //   Shifter Operation
  //   Logical Operation Unit
endmodule

module Comparator (
  input  [31:0] A,
  input  [31:0] B,
  output OUTPUT
);

  Comparator_part #(.width(32), .mode("unsigned")) comparator_1 (.a(A), .b(B), .lt(OUTPUT));  // open: gt, eq
endmodule

module Adder (
  input  [31:0] A,
  input  [31:0] B,
  input  OPCODE,
  output [31:0] OUTPUT
);

  wire [31:0] adder_1_out, subtractor_1_out;

  Adder_part #(.width(32)) adder_1 (.a(A), .b(B), .out(adder_1_out));  // open: cin, cout
  Multiplexer #(.width(32)) multiplexer_1 (
    .in0(adder_1_out), .in1(subtractor_1_out), .out(OUTPUT), .sel(OPCODE));  // open: en
  Subtractor #(.width(32)) subtractor_1 (.a(A), .b(B), .out(subtractor_1_out));  // open: bin, bout
endmodule

module _32_bit_Register_File (
  input  [4:0] RA,
  input  [4:0] RB,
  input  [4:0] RW,
  input  RegWrite,
  input  [31:0] BusW,
  output [31:0] BusA,
  output [31:0] BusB
);

  wire and_1_out, and_2_out, and_3_out, and_4_out, and_5_out, and_6_out, and_7_out, and_8_out, and_9_out,
       and_10_out, and_11_out, and_12_out, and_13_out, and_14_out, and_15_out, and_16_out, and_17_out,
       and_18_out, and_19_out, and_20_out, and_21_out, and_22_out, and_23_out, and_24_out, and_25_out,
       and_26_out, and_27_out, and_28_out, and_29_out, and_30_out, and_31_out, and_32_out, Clock_out,
       decoder_1_out0, decoder_1_out1, decoder_1_out2, decoder_1_out3, decoder_1_out4, decoder_1_out5,
       decoder_1_out6, decoder_1_out7, decoder_1_out8, decoder_1_out9, decoder_1_out10, decoder_1_out11,
       decoder_1_out12, decoder_1_out13, decoder_1_out14, decoder_1_out15, decoder_1_out16, decoder_1_out17,
       decoder_1_out18, decoder_1_out19, decoder_1_out20, decoder_1_out21, decoder_1_out22, decoder_1_out23,
       decoder_1_out24, decoder_1_out25, decoder_1_out26, decoder_1_out27, decoder_1_out28, decoder_1_out29,
       decoder_1_out30, decoder_1_out31;
  wire [31:0] register_1_q, register_2_q, register_3_q, register_4_q, register_5_q, register_6_q,
       register_7_q, register_8_q, register_9_q, register_10_q, register_11_q, register_12_q, register_13_q,
       register_14_q, register_15_q, register_16_q, register_17_q, register_18_q, register_19_q,
       register_20_q, register_21_q, register_22_q, register_23_q, register_24_q, register_25_q,
       register_26_q, register_27_q, register_28_q, register_29_q, register_30_q, register_31_q,
       register_32_q;

  Multiplexer #(.select(5), .width(32)) multiplexer_1 (
    .in0(register_1_q), .in1(register_2_q), .in2(register_3_q), .in3(register_4_q), .in4(register_5_q),
    .in5(register_6_q), .in6(register_7_q), .in7(register_8_q), .in8(register_9_q), .in9(register_10_q),
    .in10(register_11_q), .in11(register_12_q), .in12(register_13_q), .in13(register_14_q),
    .in14(register_15_q), .in15(register_16_q), .in16(register_17_q), .in17(register_18_q),
    .in18(register_19_q), .in19(register_20_q), .in20(register_21_q), .in21(register_22_q),
    .in22(register_23_q), .in23(register_24_q), .in24(register_25_q), .in25(register_26_q),
    .in26(register_27_q), .in27(register_28_q), .in28(register_29_q), .in29(register_30_q),
    .in30(register_31_q), .in31(register_32_q), .out(BusA), .sel(RA));  // open: en
  Register #(.width(32)) register_1 (.D(BusW), .en(and_1_out), .Q(register_1_q), .clk(Clock_out));  // open: clr
  Register #(.width(32)) register_2 (.D(BusW), .en(and_2_out), .Q(register_2_q), .clk(Clock_out));  // open: clr
  Register #(.width(32)) register_3 (.D(BusW), .en(and_3_out), .Q(register_3_q), .clk(Clock_out));  // open: clr
  Register #(.width(32)) register_4 (.D(BusW), .en(and_4_out), .Q(register_4_q), .clk(Clock_out));  // open: clr
  and and_1 (and_1_out, RegWrite, decoder_1_out0);
  and and_2 (and_2_out, RegWrite, decoder_1_out1);
  and and_3 (and_3_out, RegWrite, decoder_1_out2);
  and and_4 (and_4_out, RegWrite, decoder_1_out3);
  and and_5 (and_5_out, RegWrite, decoder_1_out4);
  and and_6 (and_6_out, RegWrite, decoder_1_out5);
  and and_7 (and_7_out, RegWrite, decoder_1_out6);
  and and_8 (and_8_out, RegWrite, decoder_1_out7);
  and and_9 (and_9_out, RegWrite, decoder_1_out8);
  and and_10 (and_10_out, RegWrite, decoder_1_out9);
  and and_11 (and_11_out, RegWrite, decoder_1_out10);
  and and_12 (and_12_out, RegWrite, decoder_1_out11);
  and and_13 (and_13_out, RegWrite, decoder_1_out12);
  and and_14 (and_14_out, RegWrite, decoder_1_out13);
  and and_15 (and_15_out, RegWrite, decoder_1_out14);
  and and_16 (and_16_out, RegWrite, decoder_1_out15);
  Register #(.width(32)) register_5 (.D(BusW), .en(and_5_out), .Q(register_5_q), .clk(Clock_out));  // open: clr
  Register #(.width(32)) register_6 (.D(BusW), .en(and_6_out), .Q(register_6_q), .clk(Clock_out));  // open: clr
  Register #(.width(32)) register_7 (.D(BusW), .en(and_7_out), .Q(register_7_q), .clk(Clock_out));  // open: clr
  Register #(.width(32)) register_8 (.D(BusW), .en(and_8_out), .Q(register_8_q), .clk(Clock_out));  // open: clr
  Decoder #(.select(5)) decoder_1 (
    .out0(decoder_1_out0), .out1(decoder_1_out1), .out2(decoder_1_out2), .out3(decoder_1_out3),
    .out4(decoder_1_out4), .out5(decoder_1_out5), .out6(decoder_1_out6), .out7(decoder_1_out7),
    .out8(decoder_1_out8), .out9(decoder_1_out9), .out10(decoder_1_out10), .out11(decoder_1_out11),
    .out12(decoder_1_out12), .out13(decoder_1_out13), .out14(decoder_1_out14), .out15(decoder_1_out15),
    .out16(decoder_1_out16), .out17(decoder_1_out17), .out18(decoder_1_out18), .out19(decoder_1_out19),
    .out20(decoder_1_out20), .out21(decoder_1_out21), .out22(decoder_1_out22), .out23(decoder_1_out23),
    .out24(decoder_1_out24), .out25(decoder_1_out25), .out26(decoder_1_out26), .out27(decoder_1_out27),
    .out28(decoder_1_out28), .out29(decoder_1_out29), .out30(decoder_1_out30), .out31(decoder_1_out31),
    .sel(RW));  // open: en
  Register #(.width(32)) register_9 (.D(BusW), .en(and_9_out), .Q(register_9_q), .clk(Clock_out));  // open: clr
  Register #(.width(32)) register_10 (.D(BusW), .en(and_10_out), .Q(register_10_q), .clk(Clock_out));  // open: clr
  Register #(.width(32)) register_11 (.D(BusW), .en(and_11_out), .Q(register_11_q), .clk(Clock_out));  // open: clr
  Register #(.width(32)) register_12 (.D(BusW), .en(and_12_out), .Q(register_12_q), .clk(Clock_out));  // open: clr
  Register #(.width(32)) register_13 (.D(BusW), .en(and_13_out), .Q(register_13_q), .clk(Clock_out));  // open: clr
  Register #(.width(32)) register_14 (.D(BusW), .en(and_14_out), .Q(register_14_q), .clk(Clock_out));  // open: clr
  Register #(.width(32)) register_15 (.D(BusW), .en(and_15_out), .Q(register_15_q), .clk(Clock_out));  // open: clr
  Register #(.width(32)) register_16 (.D(BusW), .en(and_16_out), .Q(register_16_q), .clk(Clock_out));  // open: clr
  Register #(.width(32)) register_17 (.D(BusW), .en(and_32_out), .Q(register_17_q), .clk(Clock_out));  // open: clr
  Register #(.width(32)) register_18 (.D(BusW), .en(and_31_out), .Q(register_18_q), .clk(Clock_out));  // open: clr
  Register #(.width(32)) register_19 (.D(BusW), .en(and_30_out), .Q(register_19_q), .clk(Clock_out));  // open: clr
  Register #(.width(32)) register_20 (.D(BusW), .en(and_29_out), .Q(register_20_q), .clk(Clock_out));  // open: clr
  Register #(.width(32)) register_21 (.D(BusW), .en(and_28_out), .Q(register_21_q), .clk(Clock_out));  // open: clr
  Register #(.width(32)) register_22 (.D(BusW), .en(and_27_out), .Q(register_22_q), .clk(Clock_out));  // open: clr
  Register #(.width(32)) register_23 (.D(BusW), .en(and_26_out), .Q(register_23_q), .clk(Clock_out));  // open: clr
  Register #(.width(32)) register_24 (.D(BusW), .en(and_25_out), .Q(register_24_q), .clk(Clock_out));  // open: clr
  Register #(.width(32)) register_25 (.D(BusW), .en(and_24_out), .Q(register_25_q), .clk(Clock_out));  // open: clr
  Register #(.width(32)) register_26 (.D(BusW), .en(and_23_out), .Q(register_26_q), .clk(Clock_out));  // open: clr
  Register #(.width(32)) register_27 (.D(BusW), .en(and_22_out), .Q(register_27_q), .clk(Clock_out));  // open: clr
  Register #(.width(32)) register_28 (.D(BusW), .en(and_21_out), .Q(register_28_q), .clk(Clock_out));  // open: clr
  and and_17 (and_17_out, RegWrite, decoder_1_out31);
  and and_18 (and_18_out, RegWrite, decoder_1_out30);
  and and_19 (and_19_out, RegWrite, decoder_1_out29);
  and and_20 (and_20_out, RegWrite, decoder_1_out28);
  and and_21 (and_21_out, RegWrite, decoder_1_out27);
  and and_22 (and_22_out, RegWrite, decoder_1_out26);
  and and_23 (and_23_out, RegWrite, decoder_1_out25);
  and and_24 (and_24_out, RegWrite, decoder_1_out24);
  and and_25 (and_25_out, RegWrite, decoder_1_out23);
  and and_26 (and_26_out, RegWrite, decoder_1_out22);
  and and_27 (and_27_out, RegWrite, decoder_1_out21);
  and and_28 (and_28_out, RegWrite, decoder_1_out20);
  and and_29 (and_29_out, RegWrite, decoder_1_out19);
  and and_30 (and_30_out, RegWrite, decoder_1_out18);
  and and_31 (and_31_out, RegWrite, decoder_1_out17);
  and and_32 (and_32_out, RegWrite, decoder_1_out16);
  Register #(.width(32)) register_29 (.D(BusW), .en(and_20_out), .Q(register_29_q), .clk(Clock_out));  // open: clr
  Register #(.width(32)) register_30 (.D(BusW), .en(and_19_out), .Q(register_30_q), .clk(Clock_out));  // open: clr
  Register #(.width(32)) register_31 (.D(BusW), .en(and_18_out), .Q(register_31_q), .clk(Clock_out));  // open: clr
  Register #(.width(32)) register_32 (.D(BusW), .en(and_17_out), .Q(register_32_q), .clk(Clock_out));  // open: clr
  Multiplexer #(.select(5), .width(32)) multiplexer_2 (
    .in0(register_1_q), .in1(register_2_q), .in2(register_3_q), .in3(register_4_q), .in4(register_5_q),
    .in5(register_6_q), .in6(register_7_q), .in7(register_8_q), .in8(register_9_q), .in9(register_10_q),
    .in10(register_11_q), .in11(register_12_q), .in12(register_13_q), .in13(register_14_q),
    .in14(register_15_q), .in15(register_16_q), .in16(register_17_q), .in17(register_18_q),
    .in18(register_19_q), .in19(register_20_q), .in20(register_21_q), .in21(register_22_q),
    .in22(register_23_q), .in23(register_24_q), .in24(register_25_q), .in25(register_26_q),
    .in26(register_27_q), .in27(register_28_q), .in28(register_29_q), .in29(register_30_q),
    .in30(register_31_q), .in31(register_32_q), .out(BusB), .sel(RB));  // open: en
  Clock Clock (.out(Clock_out));

  // Notes on the sheet:
  //   Least SIgnificant Register
  //   Most Significant Register
endmodule

module Chip (
  input  [23:0] Address,
  input  [7:0] Input,
  input  Store,
  input  Chip_enable,
  input  Clock,
  input  Load,
  input  Clear,
  output [7:0] Output
);

  RAM #(.addrWidth(24), .bus("separate")) ram_1 (
    .addr(Address), .din(Input), .data(Output), .str(Store), .sel(Chip_enable), .clk(Clock), .ld(Load),
    .clr(Clear));
endmodule

module Module (
  input  [23:0] Address,
  input  [7:0] Input,
  input  Store,
  input  Clock,
  input  Load,
  input  Clear,
  input  [1:0] Chip_select,
  input  Module_enable,
  output [7:0] Output_2,
  output [7:0] Output_0,
  output [7:0] Output_3,
  output [7:0] Output_1
);

  wire decoder_1_out0, decoder_1_out1, decoder_1_out2, decoder_1_out3, undriven;

  Decoder #(.select(2)) decoder_1 (
    .out0(decoder_1_out0), .out1(decoder_1_out1), .out2(decoder_1_out2), .out3(decoder_1_out3),
    .sel(Chip_select), .en(undriven));
  Chip Chip_3 (
    .Address(Address), .Input(Input), .Store(Store), .Chip_enable(decoder_1_out3), .Clock(Clock),
    .Load(Load), .Clear(Clear), .Output(Output_3));
  Chip Chip_2 (
    .Address(Address), .Input(Input), .Store(Store), .Chip_enable(decoder_1_out2), .Clock(Clock),
    .Load(Load), .Clear(Clear), .Output(Output_2));
  Chip Chip_1 (
    .Address(Address), .Input(Input), .Store(Store), .Chip_enable(decoder_1_out1), .Clock(Clock),
    .Load(Load), .Clear(Clear), .Output(Output_1));
  Chip Chip_0 (
    .Address(Address), .Input(Input), .Store(Store), .Chip_enable(decoder_1_out0), .Clock(Clock),
    .Load(Load), .Clear(Clear), .Output(Output_0));
endmodule

module Bank (
  input  [1:0] Module_Enable,
  input  [1:0] Module_Enable_2,
  input  [1:0] Module_Enable_3,
  input  [1:0] Module_Enable_4,
  input  [1:0] Module_Enable_5,
  input  [1:0] Module_Enable_6,
  input  [1:0] Module_enable_7,
  input  [1:0] Module_enable_8,
  input  Store,
  input  Clock,
  input  Load,
  input  Clear,
  input  [7:0] Input,
  input  [23:0] Addres,
  input  [2:0] Select_Module,
  input  Bank_enable,
  output [7:0] out_17,
  output [7:0] out_18,
  output [7:0] out_19,
  output [7:0] out_20,
  output [7:0] out_21,
  output [7:0] out_22,
  output [7:0] out_23,
  output [7:0] out_24,
  output [7:0] out_25,
  output [7:0] out_26,
  output [7:0] out_27,
  output [7:0] out_28,
  output [7:0] out_29,
  output [7:0] out_30,
  output [7:0] out_31,
  output [7:0] out_32,
  output [7:0] out_33,
  output [7:0] out_34,
  output [7:0] out_35,
  output [7:0] out_36,
  output [7:0] out_37,
  output [7:0] out_38,
  output [7:0] out_39,
  output [7:0] out_40,
  output [7:0] out_41,
  output [7:0] out_42,
  output [7:0] out_43,
  output [7:0] out_44,
  output [7:0] out_45,
  output [7:0] out_46,
  output [7:0] out_47,
  output [7:0] out_48
);

  wire Module_0, Module_1, Module_2, Module_3, Module_4, Module_5, Module_6, Module_7;

  Module u_Module_7 (
    .Address(Addres), .Input(Input), .Store(Store), .Clock(Clock), .Load(Clock), .Clear(Clear),
    .Module_enable(Module_7), .Chip_select(Module_enable_8), .Output_3(out_30), .Output_2(out_38),
    .Output_1(out_44), .Output_0(out_48));
  Module u_Module_6 (
    .Address(Addres), .Input(Input), .Store(Store), .Clock(Clock), .Load(Clock), .Clear(Clear),
    .Module_enable(Module_6), .Chip_select(Module_enable_7), .Output_3(out_29), .Output_2(out_36),
    .Output_1(out_42), .Output_0(out_47));
  Module u_Module_5 (
    .Address(Addres), .Input(Input), .Store(Store), .Clock(Clock), .Load(Clock), .Clear(Clear),
    .Module_enable(Module_5), .Chip_select(Module_Enable_6), .Output_3(out_25), .Output_2(out_31),
    .Output_1(out_39), .Output_0(out_45));
  Module u_Module_4 (
    .Address(Addres), .Input(Input), .Store(Store), .Clock(Clock), .Load(Clock), .Clear(Clear),
    .Module_enable(Module_4), .Chip_select(Module_Enable), .Output_3(out_20), .Output_2(out_26),
    .Output_1(out_32), .Output_0(out_46));
  Decoder #(.select(3)) decoder_1 (
    .out0(Module_0), .out1(Module_1), .out2(Module_2), .out3(Module_3), .out4(Module_4), .out5(Module_5),
    .out6(Module_6), .out7(Module_7), .sel(Select_Module), .en(Bank_enable));
  Module u_Module_3 (
    .Address(Addres), .Input(Input), .Store(Store), .Clock(Clock), .Load(Clock), .Clear(Clear),
    .Module_enable(Module_3), .Chip_select(Module_Enable_2), .Output_3(out_21), .Output_2(out_24),
    .Output_1(out_37), .Output_0(out_43));
  Module u_Module_2 (
    .Address(Addres), .Input(Input), .Store(Store), .Clock(Clock), .Load(Clock), .Clear(Clear),
    .Module_enable(Module_2), .Chip_select(Module_Enable_3), .Output_3(out_17), .Output_2(out_22),
    .Output_1(out_33), .Output_0(out_40));
  Module u_Module_1 (
    .Address(Addres), .Input(Input), .Store(Store), .Clock(Clock), .Load(Clock), .Clear(Clear),
    .Module_enable(Module_1), .Chip_select(Module_Enable_4), .Output_3(out_18), .Output_2(out_27),
    .Output_1(out_34), .Output_0(out_41));
  Module u_Module_0 (
    .Address(Addres), .Input(Input), .Store(Store), .Clock(Clock), .Load(Clock), .Clear(Clear),
    .Module_enable(Module_0), .Chip_select(Module_Enable_5), .Output_3(out_19), .Output_2(out_23),
    .Output_1(out_28), .Output_0(out_35));

  assign Load = Clock;

  // Other names for the same wires on the sheet: address[23:0] = Addres
endmodule

module _4GB_RAM (
  input  [31:0] Address
);

  Decoder #(.select(3)) decoder_1 (.sel(Address[31:29]));  // open: out0, out1, out2, out3, out4, out5, out6, out7, en
  Bank Bank_0 ();  // open: Module_Enable, Module_Enable_2, Module_Enable_3, Module_Enable_4, Module_Enable_5, Module_Enable_6, Module_enable_7, Module_enable_8, Select_Module, Bank_enable, Addres, Input, Store, Clock, Load, Clear, out_30, out_38, out_44, out_48, out_29, out_36, out_42, out_47, out_25, out_31, out_39, out_20, out_45, out_26, out_32, out_46, out_21, out_24, out_37, out_43, out_17, out_22, out_33, out_40, out_18, out_27, out_34, out_19, out_41, out_23, out_28, out_35
  Bank Bank_3 ();  // open: Module_Enable, Module_Enable_2, Module_Enable_3, Module_Enable_4, Module_Enable_5, Module_Enable_6, Module_enable_7, Module_enable_8, Select_Module, Bank_enable, Addres, Input, Store, Clock, Load, Clear, out_30, out_38, out_44, out_48, out_29, out_36, out_42, out_47, out_25, out_31, out_39, out_20, out_45, out_26, out_32, out_46, out_21, out_24, out_37, out_43, out_17, out_22, out_33, out_40, out_18, out_27, out_34, out_19, out_41, out_23, out_28, out_35
  Bank Bank_1 ();  // open: Module_Enable, Module_Enable_2, Module_Enable_3, Module_Enable_4, Module_Enable_5, Module_Enable_6, Module_enable_7, Module_enable_8, Select_Module, Bank_enable, Addres, Input, Store, Clock, Load, Clear, out_30, out_38, out_44, out_48, out_29, out_36, out_42, out_47, out_25, out_31, out_39, out_20, out_45, out_26, out_32, out_46, out_21, out_24, out_37, out_43, out_17, out_22, out_33, out_40, out_18, out_27, out_34, out_19, out_41, out_23, out_28, out_35
  Bank Bank_4 ();  // open: Module_Enable, Module_Enable_2, Module_Enable_3, Module_Enable_4, Module_Enable_5, Module_Enable_6, Module_enable_7, Module_enable_8, Select_Module, Bank_enable, Addres, Input, Store, Clock, Load, Clear, out_30, out_38, out_44, out_48, out_29, out_36, out_42, out_47, out_25, out_31, out_39, out_20, out_45, out_26, out_32, out_46, out_21, out_24, out_37, out_43, out_17, out_22, out_33, out_40, out_18, out_27, out_34, out_19, out_41, out_23, out_28, out_35
  Bank Bank_6 ();  // open: Module_Enable, Module_Enable_2, Module_Enable_3, Module_Enable_4, Module_Enable_5, Module_Enable_6, Module_enable_7, Module_enable_8, Select_Module, Bank_enable, Addres, Input, Store, Clock, Load, Clear, out_30, out_38, out_44, out_48, out_29, out_36, out_42, out_47, out_25, out_31, out_39, out_20, out_45, out_26, out_32, out_46, out_21, out_24, out_37, out_43, out_17, out_22, out_33, out_40, out_18, out_27, out_34, out_19, out_41, out_23, out_28, out_35
  Bank Bank_2 ();  // open: Module_Enable, Module_Enable_2, Module_Enable_3, Module_Enable_4, Module_Enable_5, Module_Enable_6, Module_enable_7, Module_enable_8, Select_Module, Bank_enable, Addres, Input, Store, Clock, Load, Clear, out_30, out_38, out_44, out_48, out_29, out_36, out_42, out_47, out_25, out_31, out_39, out_20, out_45, out_26, out_32, out_46, out_21, out_24, out_37, out_43, out_17, out_22, out_33, out_40, out_18, out_27, out_34, out_19, out_41, out_23, out_28, out_35
  Bank Bank_5 ();  // open: Module_Enable, Module_Enable_2, Module_Enable_3, Module_Enable_4, Module_Enable_5, Module_Enable_6, Module_enable_7, Module_enable_8, Select_Module, Bank_enable, Addres, Input, Store, Clock, Load, Clear, out_30, out_38, out_44, out_48, out_29, out_36, out_42, out_47, out_25, out_31, out_39, out_20, out_45, out_26, out_32, out_46, out_21, out_24, out_37, out_43, out_17, out_22, out_33, out_40, out_18, out_27, out_34, out_19, out_41, out_23, out_28, out_35
  Bank Bank_7 ();  // open: Module_Enable, Module_Enable_2, Module_Enable_3, Module_Enable_4, Module_Enable_5, Module_Enable_6, Module_enable_7, Module_enable_8, Select_Module, Bank_enable, Addres, Input, Store, Clock, Load, Clear, out_30, out_38, out_44, out_48, out_29, out_36, out_42, out_47, out_25, out_31, out_39, out_20, out_45, out_26, out_32, out_46, out_21, out_24, out_37, out_43, out_17, out_22, out_33, out_40, out_18, out_27, out_34, out_19, out_41, out_23, out_28, out_35

  // Other names for the same wires on the sheet: Select[1:0] = Address[1:0]; Address_t[23:0] = Address[25:2];
  //   Select_Module[2:0] = Address[28:26]
endmodule
